# Fritzing sketch schematic (saved by Fritzing 0.9.3b)
breadboards: 1

parts:
  Част1 = Arduino Uno (Rev3)
  Grove1 = Grove OLED 128x96
  RHT1 = Humidity and Temperature Sensor RHT03
  Част2 = Soil Moisture Sensor
  Q1 = NPN-Transistor [package="TO92 [THT]"]
  R1 = Resistor [tolerance=±5% resistance=360 package="2010 [SMD]"]
  M1 = DC Motor
  R2 = Resistor [tolerance=±5% resistance=1.8k package="2010 [SMD]"]

nets:
  N1: Част1.A0, Част2.SIG
  N2: Част1.A4/SDA, Grove1.SDA
  N3: Част1.A5/SCL, Grove1.SCL
  GND: Част1.GND, Grove1.GND, RHT1.GND_2, Част2.GND, M1.pin_1
  N4: Част1.D4, RHT1.Data-signal
  3V3: Част1.3V3, Grove1.VCC
  VCC: Част1.5V, RHT1.Vcc, Част2.VCC, Q1.B, R2.Pin_0, R2.Pin_1
  N5: Q1.E, R1.Pin_1
  N6: Q1.C, M1.pin_2
